# Fritzing sketch 7segment-display (saved by Fritzing 0.9.3b)
breadboards: 1

parts:
  元件1 = Arduino Nano (Rev3.0)
  R1 = Resistor [tolerance=±5% resistance=220 package=THT]  # not connected
  S1 = Pushbutton [package="[THT]"]
  S2 = Pushbutton [package="[THT]"]
  R2 = Resistor [tolerance=±5% resistance=220 package=THT]
  R3 = Resistor [tolerance=±5% resistance=220 package=THT]
  LED1 = LED - 5mm [color="Green (555nm)" package="5 mm [THT]"]
  LED2 = LED - 5mm [color="Red (633nm)" package="5 mm [THT]"]
  R4 = Resistor [tolerance=±5% resistance=220 package=THT]
  DI1 = 7-Segment LED Display [package=THT]
  Mod1 = KY-015 Temperature & Humidity Sensor Module [package="Breakout board"]

nets:
  N1: 元件1.GND, S1.Pin_1, S1.Pin_2, S2.Pin_1, S2.Pin_2, Mod1.S
  N2: 元件1.D2, DI1.cathodeA
  N3: 元件1.D3, DI1.cathodeB
  N4: 元件1.D4, DI1.cathodeC
  N5: 元件1.D5, DI1.cathodeD
  N6: 元件1.D6, DI1.cathodeE
  N7: 元件1.D7, DI1.cathodeF
  N8: 元件1.D8, DI1.cathodeG
  N9: 元件1.D11/MOSI, LED2.cathode
  N10: 元件1.D12/MISO, LED1.cathode
  N11: 元件1.5V, R2.Pin_1, R3.Pin_1, R4.Pin_1, Mod1.-
  N12: 元件1.A4, Mod1.Vin
  N13: 元件1.A3, S2.Pin_3, S2.Pin_4, R3.Pin_0
  N14: 元件1.A2, S1.Pin_3, S1.Pin_4, R2.Pin_0
  N15: LED1.anode, LED2.anode, R4.Pin_0

custom parts:
  KY-015 Temperature & Humidity Sensor Module: KY-015 temperature and humidity sensor module, provides a low-latency serial interface to measure humidity and temperature.
